# Fritzing sketch iot_attendance_connections (saved by Fritzing 0.9.3b)
breadboards: 1

parts:
  Part2 = RFID-RC522-v2
  U3 = NodeMCU V3.0
  J1 = Piezo Speaker

nets:
  N1: Part2.SDA, U3.D4
  N2: Part2.SCK, U3.D5
  N3: Part2.MOSI, U3.D7
  N4: Part2.MISO, U3.D6
  GND: Part2.GND, U3.GND, J1.pin1
  N5: Part2.RST, U3.D3
  N6: Part2.3_3V, U3.3V3
  N7: U3.D2, J1.pin2

notes:
  RFID - NodeMCU
  SDA ==> D4
  SCK ==> D5
  MOSI ==> D7
  MISO ==> D6
  IRQ
  GND ==> GND
  RST ==> D3
  3.3V ==> 3.3V

custom parts:
  RFID-RC522-v2: A simple China made RFID-RC522 Reader; do check the pin labels, as this is a MFRC522 based clone.
  NodeMCU V3.0: ESP8266 based NodeMCU
